# Fritzing sketch CrowsNest (saved by Fritzing 0.9.2b)
circuit board: 7.53921cm x 1.84768cm
breadboards: 1

parts:
  D1 = LTE-302 [package=lte-302]
  D2 = LTE-302 [package=lte-302]
  D3 = LTE-302 [package=lte-302]
  -/+ = female pin header, 2 pins [form="♀ (female)"]
  R/B/Y/G = female pin header, 2 pins [form="♀ (female)"]
  Wind_2 = female pin header, 2 pins [form="♀ (female)"]
  JP3 = Blend Micro Side 1 [package=1x16_machine-pin-header_lock.004]
  JP4 = Blend Micro Side 2 [package=1x16_machine-pin-header_lock.004]
  MPU-6050 = Generic female header - 2 pins [form="♀ (female)" package=THT]
  J6 = Generic female header - 2 pins [form="♀ (female)" package=THT]
  J7 = Generic female header - 2 pins [form="♀ (female)" package=THT]  # not connected
  J8 = Generic female header - 2 pins [form="♀ (female)" package=THT]
  R3 = Resistor [tolerance=±5% resistance=220 package=THT]
  R4 = Resistor [tolerance=±5% resistance=220 package=THT]

nets:
  GND: D1.A, D2.A, D3.A, JP3.GND, MPU-6050.gnd, R3.Pin_0, R4.Pin_0
  N1: D1.C, JP3.13
  N2: D2.C, JP3.12
  N3: D3.C, JP3.10
  N4: -/+.pin1, JP4.VIN
  N5: -/+.pin2, JP4.GND#1
  N6: R/B/Y/G.pin1, R/B/Y/G.pin2, JP3.V33, MPU-6050.vcc
  N7: Wind_2.pin1, JP4.0, R3.Pin_1
  N8: Wind_2.pin2, JP4.1, R4.Pin_1
  N9: JP4.2, J6.sda
  N10: JP4.3, J6.scl
  N11: JP4.5, J8.ado

notes:
  [write your note here

custom parts:
  Blend Micro Side 1: 1x16 .1 header
  Blend Micro Side 2: 1x16 .1 header
  Generic female header - 2 pins: Generic female header
  Generic female header - 2 pins: Generic female header
  Generic female header - 2 pins: Generic female header
  Generic female header - 2 pins: Generic female header
