# Fritzing sketch MrGibbs (saved by Fritzing 0.9.2b)
circuit board: 6.23489cm x 3.23679cm
breadboards: 1

parts:
  Pair = Pushbutton [package="[SMD]"]
  -/+_5v = female pin header, 2 pins [form="♀ (female)"]
  i2c = female pin header, 2 pins [form="♀ (female)"]
  3_3v = female pin header, 2 pins [form="♀ (female)"]
  GPS = Generic female header - 2 pins [form="♀ (female)" package=THT]
  GPS_2 = Generic female header - 2 pins [form="♀ (female)" package=THT]
  MPU-6050 = Generic female header - 2 pins [form="♀ (female)" package=THT]
  accel-2 = Generic female header - 2 pins [form="♀ (female)" package=THT]
  accel-3 = Generic female header - 2 pins [form="♀ (female)" package=THT]  # not connected
  accel-4 = Generic female header - 2 pins [form="♀ (female)" package=THT]
  HMC5883L = Generic female header - 2 pins [form="♀ (female)" package=THT]
  compass-2 = Generic female header - 2 pins [form="♀ (female)" package=THT]
  5v/3_3v = female pin header, 2 pins [form="♀ (female)"]
  J2 = female pin header, 2 pins [form="♀ (female)"]
  J3 = female pin header, 2 pins [form="♀ (female)"]
  J4 = female pin header, 2 pins [form="♀ (female)"]
  J5 = female pin header, 2 pins [form="♀ (female)"]
  J6 = female pin header, 2 pins [form="♀ (female)"]  # not connected
  J7 = female pin header, 2 pins [form="♀ (female)"]  # not connected
  J8 = female pin header, 2 pins [form="♀ (female)"]  # not connected
  J9 = female pin header, 2 pins [form="♀ (female)"]  # not connected
  J10 = female pin header, 2 pins [form="♀ (female)"]  # not connected
  J11 = female pin header, 2 pins [form="♀ (female)"]  # not connected
  J12 = female pin header, 2 pins [form="♀ (female)"]  # not connected
  J13 = female pin header, 2 pins [form="♀ (female)"]  # not connected
  J14 = female pin header, 2 pins [form="♀ (female)"]  # not connected
  J15 = female pin header, 2 pins [form="♀ (female)"]  # not connected
  J16 = female pin header, 2 pins [form="♀ (female)"]  # not connected
  J17 = female pin header, 2 pins [form="♀ (female)"]
  J22 = female pin header, 2 pins [form="♀ (female)"]
  J26 = female pin header, 2 pins [form="♀ (female)"]  # not connected
  J27 = female pin header, 2 pins [form="♀ (female)"]
  On/Off = Toggle Switch [package=THT]

nets:
  N1: Pair.Pin_1, Pair.Pin_2, J27.pin2
  VCC: Pair.Pin_3, Pair.Pin_4, 3_3v.pin2, GPS.vcc, MPU-6050.vcc, HMC5883L.vcc, 5v/3_3v.pin2
  N2: -/+_5v.pin1, On/Off.L2
  GND: -/+_5v.pin2, 3_3v.pin1, GPS_2.gnd, MPU-6050.gnd, HMC5883L.gnd, J5.pin2
  N3: i2c.pin1, accel-2.sda, compass-2.sda, J2.pin2
  N4: i2c.pin2, accel-2.scl, compass-2.scl, J3.pin2
  N5: GPS.rx, J4.pin1
  N6: GPS_2.tx, J5.pin1
  N7: accel-4.ado, J17.pin2
  N8: accel-4.int, J22.pin2
  N9: 5v/3_3v.pin1, On/Off.COM

custom parts:
  Generic female header - 2 pins: Generic female header
  Generic female header - 2 pins: Generic female header
  Generic female header - 2 pins: Generic female header
  Generic female header - 2 pins: Generic female header
  Generic female header - 2 pins: Generic female header
  Generic female header - 2 pins: Generic female header
  Generic female header - 2 pins: Generic female header
  Generic female header - 2 pins: Generic female header
